// Logisim project Lab1.circ as structural Verilog: 9 circuits, main circuit main
module main (
);

  wire branchunit_1_branch_taken, Clock, IsBranch, maincontrol_1_alusrc, maincontrol_1_memwrite, MemRead,
       RegWrite;
  wire [1:0] maincontrol_1_aluop;
  wire [2:0] ext3, ImmSel;
  wire [3:0] ALUCrtl;
  wire [4:0] instructiondecode_1_rd, instructiondecode_1_rs1, instructiondecode_1_rs2;
  wire [6:0] funct7, instructiondecode_1_op;
  wire [31:0] adder_2_out, alu_1_result, immgen_1_imm, memory_1_readdata, multiplexer_2_out,
       multiplexer_3_out, PC, PC_4, registerfile_1_rs1_data, registerfile_1_rs2_data, rom_1_data;

  Clock clock_1 (.out(Clock));
  Register #(.width(32)) register_1 (.D(PC_4), .clk(Clock), .Q(PC));  // open: en, clr
  Adder #(.width(32)) adder_1 (.a(PC), .b(32'h4), .out(PC_4));  // open: cin, cout
  ROM #(.dataWidth(32)) rom_1 (.addr(PC[9:2]), .data(rom_1_data));
  // Probe on rom_1_data
  InstructionDecode instructiondecode_1 (
    .Instruction(rom_1_data), .funct7(funct7), .rs2(instructiondecode_1_rs2), .rs1(instructiondecode_1_rs1),
    .ext3(ext3), .rd(instructiondecode_1_rd), .OP(instructiondecode_1_op));
  Adder #(.width(32)) adder_2 (.a(PC), .b(multiplexer_2_out), .out(adder_2_out));  // open: cin, cout
  Multiplexer #(.width(32)) multiplexer_1 (
    .in0(PC_4), .in1(adder_2_out), .sel(branchunit_1_branch_taken));  // open: out
  RegisterFile registerfile_1 (
    .write_data(multiplexer_3_out), .clock(Clock), .rs1(instructiondecode_1_rs1),
    .rs2(instructiondecode_1_rs2), .write(RegWrite), .rd(instructiondecode_1_rd),
    .rs1_data(registerfile_1_rs1_data), .rs2_data(registerfile_1_rs2_data));
  MainControl maincontrol_1 (
    .in_1(instructiondecode_1_op), .RegWrite(RegWrite), .ALUSrc(maincontrol_1_alusrc),
    .MemWrite(maincontrol_1_memwrite), .IsBranch(IsBranch), .ALUOp(maincontrol_1_aluop), .ImmSel(ImmSel),
    .MemRead(MemRead));
  Multiplexer #(.width(32)) multiplexer_2 (
    .in0(registerfile_1_rs2_data), .in1(immgen_1_imm), .out(multiplexer_2_out), .sel(maincontrol_1_alusrc));
  ImmGen immgen_1 (.Instruction(rom_1_data), .ImmSel(ImmSel), .Imm(immgen_1_imm));  // open: in_2
  BranchUnit branchunit_1 (
    .rs1_data(registerfile_1_rs1_data), .rs2_data(registerfile_1_rs2_data), .ext3(ext3), .IsBranch(IsBranch),
    .branch_taken(branchunit_1_branch_taken));
  ALU alu_1 (
    .rs1_data(registerfile_1_rs1_data), .rs2_data(multiplexer_2_out), .ALUControl(ALUCrtl),
    .result(alu_1_result));
  ALUControl alucontrol_1 (.funct7(funct7), .ALUOp(maincontrol_1_aluop), .ext3(ext3), .ALUCtrl(ALUCrtl));
  Multiplexer #(.width(32)) multiplexer_3 (
    .in0(alu_1_result), .in1(memory_1_readdata), .out(multiplexer_3_out), .sel(MemRead));
  Memory memory_1 (
    .Address(alu_1_result), .WriteData(registerfile_1_rs2_data), .MemWrite(maincontrol_1_memwrite),
    .ext3(ext3), .MemRead(MemRead), .CLK(Clock), .ReadData(memory_1_readdata));

  // Notes on the sheet:
  //   contents of rom_1 (hex, n*v repeats v):
  //   111 ab
endmodule

module ALU (
  input  [31:0] rs1_data,
  input  [31:0] rs2_data,
  input  [3:0] ALUControl,
  output [31:0] result
);

  wire comparator_1_lt, comparator_2_lt;
  wire [31:0] adder_1_out, and_1_out, bit_extender_1_out, bit_extender_2_out, or_1_out, shifter_1_out,
       shifter_2_out, shifter_3_out, subtractor_1_out, xor_1_out;

  Adder #(.width(32)) adder_1 (.a(rs1_data), .b(rs2_data), .out(adder_1_out));  // open: cin, cout
  Subtractor #(.width(32)) subtractor_1 (.a(rs1_data), .b(rs2_data), .out(subtractor_1_out));  // open: bin, bout
  assign and_1_out = rs1_data & rs2_data;  // AND_Gate and_1, 32 bits wide
  assign or_1_out = rs1_data | rs2_data;  // OR_Gate or_1, 32 bits wide
  assign xor_1_out = rs1_data ^ rs2_data;  // XOR_Gate xor_1, 32 bits wide
  Shifter #(.width(32)) shifter_1 (.in(rs1_data), .\dist (rs2_data[4:0]), .out(shifter_1_out));
  Shifter #(.shift("lr"), .width(32)) shifter_2 (.in(rs1_data), .\dist (rs2_data[4:0]), .out(shifter_2_out));
  Shifter #(.shift("lr"), .width(32)) shifter_3 (.in(rs1_data), .\dist (rs2_data[4:0]), .out(shifter_3_out));
  Comparator #(.width(32)) comparator_1 (.a(rs1_data), .b(rs2_data), .lt(comparator_1_lt));  // open: gt, eq
  Comparator #(.mode("unsigned"), .width(32)) comparator_2 (
    .a(rs1_data), .b(rs2_data), .lt(comparator_2_lt));  // open: gt, eq
  assign bit_extender_1_out = {{31{comparator_1_lt}}, comparator_1_lt};  // Bit_Extender bit_extender_1
  assign bit_extender_2_out = {{31{comparator_2_lt}}, comparator_2_lt};  // Bit_Extender bit_extender_2
  Multiplexer #(.select(4), .width(32)) multiplexer_1 (
    .in0(adder_1_out), .in1(subtractor_1_out), .in2(and_1_out), .in3(or_1_out), .in4(xor_1_out),
    .in5(shifter_1_out), .in6(shifter_2_out), .in7(shifter_3_out), .in8(bit_extender_1_out),
    .in9(bit_extender_2_out), .out(result), .sel(ALUControl));  // open: in10, in11, in12, in13, in14, in15
endmodule

module InstructionDecode (
  input  [31:0] Instruction,
  output [6:0] funct7,
  output [4:0] rs2,
  output [4:0] rs1,
  output [2:0] ext3,
  output [4:0] rd,
  output [6:0] OP
);


  assign ext3 = Instruction[14:12];
  assign funct7 = Instruction[31:25];
  assign OP = Instruction[6:0];
  assign rd = Instruction[11:7];
  assign rs1 = Instruction[19:15];
  assign rs2 = Instruction[24:20];
endmodule

module RegisterFile (
  input  [31:0] write_data,
  input  clock,
  input  [4:0] rs1,
  input  [4:0] rs2,
  input  write,
  input  [4:0] rd,
  output [31:0] rs1_data,
  output [31:0] rs2_data
);

  wire write_E0, write_E1, write_E2, write_E3, write_E4, write_E5, write_E6, write_E7, write_E8, write_E9,
       write_E10, write_E11, write_E12, write_E13, write_E14, write_E15, write_E16, write_E17, write_E18,
       write_E19, write_E20, write_E21, write_E22, write_E23, write_E24, write_E25, write_E26, write_E27,
       write_E28, write_E29, write_E30, write_E31;
  wire [31:0] undriven, X0, X1, X2, X3, X4, X5, X6, X7, X8, X9, X10, X11, X12, X13, X14, X15, X16, X17, X18,
       X19, X20, X21, X22, X23, X24, X25, X26, X27, X28, X29, X30, X31;

  Register #(.width(32)) register_1 (.D({32{1'b0}}), .en(write_E0), .clk(clock), .Q(X0));  // open: clr
  Register #(.width(32)) register_2 (.D(write_data), .en(write_E1), .clk(clock), .Q(X1));  // open: clr
  Register #(.width(32)) register_3 (.D(write_data), .en(write_E2), .clk(clock), .Q(X2));  // open: clr
  Register #(.width(32)) register_4 (.D(write_data), .en(write_E3), .clk(clock), .Q(X3));  // open: clr
  Register #(.width(32)) register_5 (.D(write_data), .en(write_E16), .clk(clock), .Q(X16));  // open: clr
  Register #(.width(32)) register_6 (.D(write_data), .en(write_E17), .clk(clock), .Q(X17));  // open: clr
  Register #(.width(32)) register_7 (.D(write_data), .en(write_E18), .clk(clock), .Q(X18));  // open: clr
  Register #(.width(32)) register_8 (.D(write_data), .en(write_E19), .clk(clock), .Q(X19));  // open: clr
  Register #(.width(32)) register_9 (.D(write_data), .en(write_E4), .clk(clock), .Q(X4));  // open: clr
  Register #(.width(32)) register_10 (.D(write_data), .en(write_E5), .clk(clock), .Q(X5));  // open: clr
  Register #(.width(32)) register_11 (.D(write_data), .en(write_E6), .clk(clock), .Q(X6));  // open: clr
  Register #(.width(32)) register_12 (.D(write_data), .en(write_E7), .clk(clock), .Q(X7));  // open: clr
  Register #(.width(32)) register_13 (.D(undriven), .en(write_E20), .clk(clock), .Q(X20));  // open: clr
  Register #(.width(32)) register_14 (.D(write_data), .en(write_E21), .clk(clock), .Q(X21));  // open: clr
  Register #(.width(32)) register_15 (.D(write_data), .en(write_E22), .clk(clock), .Q(X22));  // open: clr
  Register #(.width(32)) register_16 (.D(write_data), .en(write_E23), .clk(clock), .Q(X23));  // open: clr
  Demultiplexer #(.select(5)) demultiplexer_1 (
    .out1(write_E1), .out2(write_E2), .out3(write_E3), .out4(write_E4), .out5(write_E5), .out6(write_E6),
    .out7(write_E7), .out8(write_E8), .out9(write_E9), .out10(write_E10), .out11(write_E11),
    .out12(write_E12), .out13(write_E13), .out14(write_E14), .out15(write_E15), .out16(write_E16),
    .out17(write_E17), .out18(write_E18), .out19(write_E19), .out20(write_E20), .out21(write_E21),
    .out22(write_E22), .out23(write_E23), .out24(write_E24), .out25(write_E25), .out26(write_E26),
    .out27(write_E27), .out28(write_E29), .out29(write_E30), .out30(write_E31), .in(write), .sel(rd));  // open: out0, out31
  Register #(.width(32)) register_17 (.D(write_data), .en(write_E8), .clk(clock), .Q(X8));  // open: clr
  Register #(.width(32)) register_18 (.D(write_data), .en(write_E9), .clk(clock), .Q(X9));  // open: clr
  Register #(.width(32)) register_19 (.D(write_data), .en(write_E10), .clk(clock), .Q(X10));  // open: clr
  Register #(.width(32)) register_20 (.D(write_data), .en(write_E11), .clk(clock), .Q(X11));  // open: clr
  Register #(.width(32)) register_21 (.D(write_data), .en(write_E24), .clk(clock), .Q(X24));  // open: clr
  Register #(.width(32)) register_22 (.D(write_data), .en(write_E25), .clk(clock), .Q(X25));  // open: clr
  Register #(.width(32)) register_23 (.D(write_data), .en(write_E26), .clk(clock), .Q(X26));  // open: clr
  Register #(.width(32)) register_24 (.D(write_data), .en(write_E27), .clk(clock), .Q(X27));  // open: clr
  Register #(.width(32)) register_25 (.D(write_data), .en(write_E12), .clk(clock), .Q(X12));  // open: clr
  Register #(.width(32)) register_26 (.D(write_data), .en(write_E13), .clk(clock), .Q(X13));  // open: clr
  Register #(.width(32)) register_27 (.D(write_data), .en(write_E14), .clk(clock), .Q(X14));  // open: clr
  Register #(.width(32)) register_28 (.D(write_data), .en(write_E15), .clk(clock), .Q(X15));  // open: clr
  Register #(.width(32)) register_29 (.D(write_data), .en(write_E28), .clk(clock), .Q(X28));  // open: clr
  Register #(.width(32)) register_30 (.D(write_data), .en(write_E29), .clk(clock), .Q(X29));  // open: clr
  Register #(.width(32)) register_31 (.D(write_data), .en(write_E30), .clk(clock), .Q(X30));  // open: clr
  Register #(.width(32)) register_32 (.D(write_data), .en(write_E31), .clk(clock), .Q(X31));  // open: clr
  Multiplexer #(.select(5), .width(32)) multiplexer_1 (
    .in0(X0), .in1(X1), .in2(X2), .in3(X3), .in4(X4), .in5(X5), .in6(X6), .in7(X7), .in8(X8), .in9(X9),
    .in10(X10), .in11(X11), .in12(X12), .in13(X13), .in14(X14), .in15(X15), .in16(X16), .in17(X17),
    .in18(X18), .in19(X19), .in20(X20), .in21(X21), .in22(X22), .in23(X23), .in24(X24), .in25(X25),
    .in26(X26), .in27(X27), .in28(X28), .in29(X29), .in30(X30), .in31(X31), .out(rs1_data), .sel(rs1));
  Multiplexer #(.select(5), .width(32)) multiplexer_2 (
    .in0(X0), .in1(X1), .in2(X2), .in3(X3), .in4(X4), .in5(X5), .in6(X6), .in7(X7), .in8(X8), .in9(X9),
    .in10(X10), .in11(X11), .in12(X12), .in13(X13), .in14(X14), .in15(X15), .in16(X16), .in17(X17),
    .in18(X18), .in19(X19), .in20(X20), .in21(X21), .in22(X22), .in23(X23), .in24(X24), .in25(X25),
    .in26(X26), .in27(X27), .in28(X28), .in29(X29), .in30(X30), .in31(X31), .out(rs2_data), .sel(rs2));

  // Other names for the same wires on the sheet: W_D[31:0] = write_data
endmodule

module ImmGen (
  input  [31:0] Instruction,
  input  in_2,
  input  [2:0] ImmSel,
  output [31:0] Imm
);

  wire [31:0] bit_extender_1_out, bit_extender_2_out, bit_extender_3_out, bit_extender_4_out;

  assign bit_extender_1_out = {{20{Instruction[31]}}, {Instruction[31:25], Instruction[11:7]}};  // Bit_Extender bit_extender_1
  assign bit_extender_2_out = {{20{Instruction[31]}}, Instruction[31:20]};  // Bit_Extender bit_extender_2
  assign bit_extender_3_out = {{19{Instruction[31]}}, {Instruction[31], Instruction[7], Instruction[30:25], Instruction[11:8], in_2}};  // Bit_Extender bit_extender_3
  assign bit_extender_4_out = {{12{Instruction[31]}}, Instruction[31:12]};  // Bit_Extender bit_extender_4
  Multiplexer #(.select(3), .width(32)) multiplexer_1 (
    .in0(bit_extender_2_out), .in1(bit_extender_1_out), .in2(bit_extender_3_out), .in3(bit_extender_4_out),
    .out(Imm), .sel(ImmSel));  // open: in4, in5, in6, in7

  // Notes on the sheet:
  //   S-Type
  //   B-Type
  //   R-Type
  //   U-type
endmodule

module MainControl (
  input  [6:0] in_1,
  output RegWrite,
  output ALUSrc,
  output MemWrite,
  output IsBranch,
  output [1:0] ALUOp,
  output [2:0] ImmSel,
  output MemRead
);

  wire IsImm, IsJAL, IsJALR, IsLui, IsR, or_4_out;

  Comparator #(.width(7)) comparator_1 (.a(in_1), .b(7'b0110011), .eq(IsR));  // open: gt, lt
  Comparator #(.width(7)) comparator_2 (.a(in_1), .b(7'b0010011), .eq(IsImm));  // open: gt, lt
  Comparator #(.width(7)) comparator_3 (.a(in_1), .b(7'b0000011), .eq(MemRead));  // open: gt, lt
  Comparator #(.width(7)) comparator_4 (.a(in_1), .b(7'b0100011), .eq(ImmSel[0]));  // open: gt, lt
  Comparator #(.width(7)) comparator_5 (.a(in_1), .b(7'b1100011), .eq(IsBranch));  // open: gt, lt
  Comparator #(.width(7)) comparator_6 (.a(in_1), .b(7'b0110111), .eq(IsLui));  // open: gt, lt
  Comparator #(.width(7)) comparator_7 (.a(in_1), .b(7'b1101111), .eq(IsJAL));  // open: gt, lt
  Comparator #(.width(7)) comparator_8 (.a(in_1), .b(7'b1100111), .eq(IsJALR));  // open: gt, lt
  or or_1 (RegWrite, IsR, IsImm, MemRead);
  or or_2 (ImmSel[1], IsBranch, IsLui);
  or or_3 (ImmSel[2], IsJAL, IsJALR);
  or or_4 (or_4_out, MemRead, IsImm, ImmSel[0]);
  or or_5 (ALUOp[0], IsBranch, IsImm);
  or or_6 (ALUOp[1], IsR, IsImm);
  or or_7 (ALUSrc, or_4_out, IsBranch);

  assign MemWrite = ImmSel[0];

  // Other names for the same wires on the sheet: IsStore = ImmSel[0]; IsLoad = MemRead
endmodule

module ALUControl (
  input  [6:0] funct7,
  input  [1:0] ALUOp,
  input  [2:0] ext3,
  output [3:0] ALUCtrl
);

  wire [3:0] multiplexer_1_out, multiplexer_2_out, multiplexer_3_out, multiplexer_4_out;

  Multiplexer #(.width(4)) multiplexer_1 (.in0(4'b0110), .in1(4'b0111), .out(multiplexer_1_out), .sel(funct7[5]));
  Multiplexer #(.width(4)) multiplexer_2 (.in0(4'b0000), .in1(4'b0001), .out(multiplexer_2_out), .sel(funct7[5]));
  Multiplexer #(.select(3), .width(4)) multiplexer_3 (
    .in0(4'b0000), .in1(4'b0101), .in2(4'b1000), .in3(4'b1001), .in4(4'b0100), .in5(multiplexer_1_out),
    .in6(4'b0011), .in7(4'b0010), .out(multiplexer_3_out), .sel(ext3));
  Multiplexer #(.select(3), .width(4)) multiplexer_4 (
    .in0(multiplexer_2_out), .in1(4'b0101), .in2(4'b1000), .in3(4'b1001), .in4(4'b0100),
    .in5(multiplexer_1_out), .in6(4'b0011), .in7(4'b0010), .out(multiplexer_4_out), .sel(ext3));
  Multiplexer #(.select(2), .width(4)) multiplexer_5 (
    .in0(4'b0000), .in1(4'b0001), .in2(multiplexer_4_out), .in3(multiplexer_3_out), .out(ALUCtrl), .sel(ALUOp));

  // Notes on the sheet:
  //   ADD
  //   SUB
endmodule

module Memory (
  input  [31:0] Address,
  input  [31:0] WriteData,
  input  MemWrite,
  input  [2:0] ext3,
  input  MemRead,
  input  CLK,
  output [31:0] ReadData
);

  wire [7:0] multiplexer_1_out;
  wire [31:0] bit_extender_1_out, bit_extender_2_out, ram_1_dout;

  RAM #(.dataWidth(32)) ram_1 (
    .addr(Address[9:2]), .we(MemWrite), .oe(MemRead), .clk(CLK), .din(WriteData), .dout(ram_1_dout));
  Multiplexer #(.select(2), .width(8)) multiplexer_1 (
    .in0(ram_1_dout[7:0]), .in1(ram_1_dout[15:8]), .in2(ram_1_dout[23:16]), .in3(ram_1_dout[31:24]),
    .out(multiplexer_1_out), .sel(Address[1:0]));
  assign bit_extender_1_out = {{24{multiplexer_1_out[7]}}, multiplexer_1_out};  // Bit_Extender bit_extender_1
  assign bit_extender_2_out = {{24{1'b0}}, multiplexer_1_out};  // Bit_Extender bit_extender_2
  Multiplexer #(.select(3), .width(32)) multiplexer_2 (
    .in0(bit_extender_1_out), .in2(ram_1_dout), .in4(bit_extender_2_out), .out(ReadData), .sel(ext3));  // open: in1, in3, in5, in6, in7

  // Notes on the sheet:
  //   lw
  //   lb
  //   lbu
endmodule

module BranchUnit (
  input  [31:0] rs1_data,
  input  [31:0] rs2_data,
  input  [2:0] ext3,
  input  IsBranch,
  output branch_taken
);

  wire comparator_1_eq, multiplexer_1_out, not_1_out;

  Comparator #(.width(32)) comparator_1 (.a(rs1_data), .b(rs2_data), .eq(comparator_1_eq));  // open: gt, lt
  not not_1 (not_1_out, comparator_1_eq);
  Multiplexer #(.select(3)) multiplexer_1 (
    .in0(comparator_1_eq), .in1(not_1_out), .out(multiplexer_1_out), .sel(ext3));  // open: in2, in3, in4, in5, in6, in7
  and and_1 (branch_taken, multiplexer_1_out, IsBranch);

  // Notes on the sheet:
  //   beq
  //   bne
endmodule
