// Logisim project alu.circ as structural Verilog: 1 circuit, main circuit ALU
module ALU (
  input  [31:0] A,
  input  [31:0] B,
  input  [3:0] ALUCtrl,
  output [31:0] Result,
  output Zero
);

  wire comparator_1_lt, comparator_2_lt;
  wire [31:0] r_add, r_and, r_or, r_sll, r_slt, r_sltu, r_sra, r_srl, r_sub, r_xor;

  Comparator #(.width(32)) comparator_1 (.a(A), .b(B), .lt(comparator_1_lt));  // open: gt, eq
  Comparator #(.mode("unsigned"), .width(32)) comparator_2 (.a(A), .b(B), .lt(comparator_2_lt));  // open: gt, eq
  Adder #(.width(32)) adder_1 (.a(A), .b(B), .out(r_add));  // open: cin, cout
  Subtractor #(.width(32)) subtractor_1 (.a(A), .b(B), .out(r_sub));  // open: bin, bout
  assign r_and = A & B;  // AND_Gate and_1, 32 bits wide
  assign r_or = A | B;  // OR_Gate or_1, 32 bits wide
  assign r_xor = A ^ B;  // XOR_Gate xor_1, 32 bits wide
  Shifter #(.width(32)) shifter_1 (.in(A), .\dist (B[4:0]), .out(r_sll));
  Shifter #(.shift("lr"), .width(32)) shifter_2 (.in(A), .\dist (B[4:0]), .out(r_srl));
  Shifter #(.shift("ar"), .width(32)) shifter_3 (.in(A), .\dist (B[4:0]), .out(r_sra));
  assign r_slt = {{31{1'b0}}, comparator_1_lt};  // Bit_Extender bit_extender_1
  assign r_sltu = {{31{1'b0}}, comparator_2_lt};  // Bit_Extender bit_extender_2
  Multiplexer #(.select(4), .width(32)) multiplexer_1 (
    .in0(r_add), .in1(r_sll), .in2(r_slt), .in3(r_sltu), .in4(r_xor), .in5(r_srl), .in6(r_or), .in7(r_and),
    .in8(r_sub), .in9({32{1'b0}}), .in10({32{1'b0}}), .in11({32{1'b0}}), .in12({32{1'b0}}), .in13(r_sra),
    .in14({32{1'b0}}), .in15(B), .out(Result), .sel(ALUCtrl));
  Comparator #(.mode("unsigned"), .width(32)) comparator_3 (.a(Result), .b({32{1'b0}}), .eq(Zero));  // open: gt, lt

  // Other names for the same wires on the sheet: shamt[4:0] = B[4:0]
endmodule
