// Logisim project branch_comp.circ as structural Verilog: 1 circuit, main circuit main
module main (
  input  [31:0] A,
  input  [31:0] B,
  input  Branch,
  input  [2:0] funct3,
  output Taken
);

  wire eq, ge, geu, lt, ltu, multiplexer_1_out, ne;

  Comparator #(.width(32)) comparator_1 (.a(A), .b(B), .eq(eq), .lt(lt));  // open: gt
  Comparator #(.mode("unsigned"), .width(32)) comparator_2 (.a(A), .b(B), .lt(ltu));  // open: gt, eq
  not not_1 (ne, eq);
  not not_2 (ge, lt);
  not not_3 (geu, ltu);
  Multiplexer #(.select(3)) multiplexer_1 (
    .in0(eq), .in1(ne), .in2(1'b0), .in3(1'b0), .in4(lt), .in5(ge), .in6(ltu), .in7(geu),
    .out(multiplexer_1_out), .sel(funct3));
  and and_1 (Taken, multiplexer_1_out, Branch);
endmodule
