// Logisim project immgen.circ as structural Verilog: 1 circuit, main circuit main
module main (
  input  [31:0] Inst,
  input  [2:0] ImmSel,
  output [31:0] Imm
);

  wire [31:0] immB, immI, immJ, immS;

  assign immI = {{20{Inst[31]}}, Inst[31:20]};  // Bit_Extender bit_extender_1
  assign immS = {{20{Inst[31]}}, {Inst[31:25], Inst[11:7]}};  // Bit_Extender bit_extender_2
  assign immB = {{19{Inst[31]}}, {Inst[31], Inst[7], Inst[30:25], Inst[11:8], 1'b0}};  // Bit_Extender bit_extender_3
  assign immJ = {{11{Inst[31]}}, {Inst[31], Inst[19:12], Inst[20], Inst[30:21], 1'b0}};  // Bit_Extender bit_extender_4
  Multiplexer #(.select(3), .width(32)) multiplexer_1 (
    .in0(immI), .in1(immS), .in2(immB), .in3({Inst[31:12], {12{1'b0}}}), .in4(immJ), .in5({32{1'b0}}),
    .in6({32{1'b0}}), .in7({32{1'b0}}), .out(Imm), .sel(ImmSel));

  // Other names for the same wires on the sheet: i11_8[3:0] = Inst[11:8]; i7 = Inst[7]; i19_12[7:0] = Inst[19:12];
  //   immU[31:12] = Inst[31:12]; i20 = Inst[20]; i24_21[3:0] = Inst[24:21]; i30_25[5:0] = Inst[30:25]; i31 = Inst[31]
endmodule
