// Logisim project regfile.circ as structural Verilog: 1 circuit, main circuit main
module main (
  input  clk,
  input  reset,
  input  RegWrite,
  input  [4:0] rs1,
  input  [4:0] rs2,
  input  [4:0] rd,
  input  [31:0] WriteData,
  output [31:0] ReadData1,
  output [31:0] ReadData2
);

  wire we1, we2, we3, we4, we5, we6, we7, we8, we9, we10, we11, we12, we13, we14, we15, we16, we17, we18,
       we19, we20, we21, we22, we23, we24, we25, we26, we27, we28, we29, we30, we31;
  wire [31:0] x1, x2, x3, x4, x5, x6, x7, x8, x9, x10, x11, x12, x13, x14, x15, x16, x17, x18, x19, x20, x21,
       x22, x23, x24, x25, x26, x27, x28, x29, x30, x31;

  Decoder #(.select(5)) decoder_1 (
    .out1(we1), .out2(we2), .out3(we3), .out4(we4), .out5(we5), .out6(we6), .out7(we7), .out8(we8),
    .out9(we9), .out10(we10), .out11(we11), .out12(we12), .out13(we13), .out14(we14), .out15(we15),
    .out16(we16), .out17(we17), .out18(we18), .out19(we19), .out20(we20), .out21(we21), .out22(we22),
    .out23(we23), .out24(we24), .out25(we25), .out26(we26), .out27(we27), .out28(we28), .out29(we29),
    .out30(we30), .out31(we31), .sel(rd), .en(RegWrite));  // open: out0
  Multiplexer #(.select(5), .width(32)) multiplexer_1 (
    .in0({32{1'b0}}), .in1(x1), .in2(x2), .in3(x3), .in4(x4), .in5(x5), .in6(x6), .in7(x7), .in8(x8),
    .in9(x9), .in10(x10), .in11(x11), .in12(x12), .in13(x13), .in14(x14), .in15(x15), .in16(x16), .in17(x17),
    .in18(x18), .in19(x19), .in20(x20), .in21(x21), .in22(x22), .in23(x23), .in24(x24), .in25(x25),
    .in26(x26), .in27(x27), .in28(x28), .in29(x29), .in30(x30), .in31(x31), .out(ReadData1), .sel(rs1));
  Register #(.width(32)) u_x1 (.D(WriteData), .en(we1), .clk(clk), .Q(x1), .clr(reset));
  Register #(.width(32)) u_x2 (.D(WriteData), .en(we2), .clk(clk), .Q(x2), .clr(reset));
  Register #(.width(32)) u_x3 (.D(WriteData), .en(we3), .clk(clk), .Q(x3), .clr(reset));
  Register #(.width(32)) u_x4 (.D(WriteData), .en(we4), .clk(clk), .Q(x4), .clr(reset));
  Register #(.width(32)) u_x5 (.D(WriteData), .en(we5), .clk(clk), .Q(x5), .clr(reset));
  Register #(.width(32)) u_x6 (.D(WriteData), .en(we6), .clk(clk), .Q(x6), .clr(reset));
  Register #(.width(32)) u_x7 (.D(WriteData), .en(we7), .clk(clk), .Q(x7), .clr(reset));
  Register #(.width(32)) u_x8 (.D(WriteData), .en(we8), .clk(clk), .Q(x8), .clr(reset));
  Register #(.width(32)) u_x9 (.D(WriteData), .en(we9), .clk(clk), .Q(x9), .clr(reset));
  Register #(.width(32)) u_x10 (.D(WriteData), .en(we10), .clk(clk), .Q(x10), .clr(reset));
  Register #(.width(32)) u_x11 (.D(WriteData), .en(we11), .clk(clk), .Q(x11), .clr(reset));
  Register #(.width(32)) u_x12 (.D(WriteData), .en(we12), .clk(clk), .Q(x12), .clr(reset));
  Register #(.width(32)) u_x13 (.D(WriteData), .en(we13), .clk(clk), .Q(x13), .clr(reset));
  Register #(.width(32)) u_x14 (.D(WriteData), .en(we14), .clk(clk), .Q(x14), .clr(reset));
  Register #(.width(32)) u_x15 (.D(WriteData), .en(we15), .clk(clk), .Q(x15), .clr(reset));
  Multiplexer #(.select(5), .width(32)) multiplexer_2 (
    .in0({32{1'b0}}), .in1(x1), .in2(x2), .in3(x3), .in4(x4), .in5(x5), .in6(x6), .in7(x7), .in8(x8),
    .in9(x9), .in10(x10), .in11(x11), .in12(x12), .in13(x13), .in14(x14), .in15(x15), .in16(x16), .in17(x17),
    .in18(x18), .in19(x19), .in20(x20), .in21(x21), .in22(x22), .in23(x23), .in24(x24), .in25(x25),
    .in26(x26), .in27(x27), .in28(x28), .in29(x29), .in30(x30), .in31(x31), .out(ReadData2), .sel(rs2));
  Register #(.width(32)) u_x16 (.D(WriteData), .en(we16), .clk(clk), .Q(x16), .clr(reset));
  Register #(.width(32)) u_x17 (.D(WriteData), .en(we17), .clk(clk), .Q(x17), .clr(reset));
  Register #(.width(32)) u_x18 (.D(WriteData), .en(we18), .clk(clk), .Q(x18), .clr(reset));
  Register #(.width(32)) u_x19 (.D(WriteData), .en(we19), .clk(clk), .Q(x19), .clr(reset));
  Register #(.width(32)) u_x20 (.D(WriteData), .en(we20), .clk(clk), .Q(x20), .clr(reset));
  Register #(.width(32)) u_x21 (.D(WriteData), .en(we21), .clk(clk), .Q(x21), .clr(reset));
  Register #(.width(32)) u_x22 (.D(WriteData), .en(we22), .clk(clk), .Q(x22), .clr(reset));
  Register #(.width(32)) u_x23 (.D(WriteData), .en(we23), .clk(clk), .Q(x23), .clr(reset));
  Register #(.width(32)) u_x24 (.D(WriteData), .en(we24), .clk(clk), .Q(x24), .clr(reset));
  Register #(.width(32)) u_x25 (.D(WriteData), .en(we25), .clk(clk), .Q(x25), .clr(reset));
  Register #(.width(32)) u_x26 (.D(WriteData), .en(we26), .clk(clk), .Q(x26), .clr(reset));
  Register #(.width(32)) u_x27 (.D(WriteData), .en(we27), .clk(clk), .Q(x27), .clr(reset));
  Register #(.width(32)) u_x28 (.D(WriteData), .en(we28), .clk(clk), .Q(x28), .clr(reset));
  Register #(.width(32)) u_x29 (.D(WriteData), .en(we29), .clk(clk), .Q(x29), .clr(reset));
  Register #(.width(32)) u_x30 (.D(WriteData), .en(we30), .clk(clk), .Q(x30), .clr(reset));
  Register #(.width(32)) u_x31 (.D(WriteData), .en(we31), .clk(clk), .Q(x31), .clr(reset));
endmodule
