// Logisim project project.circ as structural Verilog: 17 circuits, main circuit PipelineCPU
module PipelineCPU (
  output halt,
  output [31:0] cycle,
  output [31:0] out_3,
  output [31:0] if_instr,
  output [31:0] id_instr,
  output [31:0] ex_instr,
  output [31:0] mem_instr,
  output [31:0] wb_instr,
  output stall,
  output flush,
  output wb_en,
  output [4:0] wb_rd,
  output [31:0] wb_data,
  output mem_we,
  output [31:0] mem_addr,
  output [31:0] mem_wdata
);

  wire clk, ex_alusrcb, ex_branch, ex_halt, ex_jal, ex_jalr, ex_link, ex_memread, ex_memwrite, ex_regwrite,
       ex_taken, fetch_en, id_alusrcb, id_branch, id_flush, id_halt, id_jal, id_jalr, id_memread,
       id_memwrite, id_regwrite, mem_halt, mem_memwrite, mem_regwrite, nstall, run, wb_load;
  wire [0:0] ex_wbsel;
  wire [1:0] ex_alusrca, fwdA, fwdB, id_aluop, id_alusrca, id_wbsel, mem_wbsel;
  wire [1:1] wb_wbsel;
  wire [2:0] ex_f3, id_f3, id_immsel;
  wire [3:0] ex_aluctrl, id_aluctrl;
  wire [4:0] ex_rd, ex_rs1, ex_rs2, id_rd, id_rs1, id_rs2, mem_rd;
  wire [6:0] id_f7, id_op;
  wire [31:0] alu_a, alu_b, cycle_next, ex_alu, ex_imm, ex_pc, ex_pc4, ex_r1, ex_r2, ex_result, ex_target,
       fa, fb, id_imm, id_pc, id_r1, id_r2, jalr_target, mem_rdata, mem_result, pc4, pc_next,
       redirect_target, rf_r1, rf_r2, wb_rdata, wb_result;

  Clock clock_1 (.out(clk));
  Register #(.width(32)) CYCLES (.D(cycle_next), .en(run), .clk(clk), .Q(cycle));  // open: clr
  not not_1 (run, halt);
  not not_2 (nstall, stall);
  Register #(.width(32)) PC (.D(pc_next), .en(fetch_en), .clk(clk), .Q(out_3));  // open: clr
  and and_1 (fetch_en, run, nstall);
  Adder #(.width(32)) adder_1 (.a(cycle), .b(32'h1), .out(cycle_next));  // open: cin, cout
  Adder #(.width(32)) adder_2 (.a(out_3), .b(32'h4), .out(pc4));  // open: cin, cout
  Multiplexer #(.width(32)) multiplexer_1 (.in0(pc4), .in1(redirect_target), .out(pc_next), .sel(flush));
  ROM #(.addrWidth(10), .dataWidth(32)) IMEM (.addr(out_3[11:2]), .data(if_instr));
  IF_ID IF_ID (.clk(clk), .en(fetch_en), .flush(flush), .pc(out_3), .instr(if_instr), .pc_q(id_pc), .instr_q(id_instr));
  InstructionDecode instructiondecode_1 (
    .Instruction(id_instr), .funct7(id_f7), .rs2(id_rs2), .rs1(id_rs1), .ext3(id_f3), .rd(id_rd), .OP(id_op));
  MainControl maincontrol_1 (
    .OP(id_op), .RegWrite(id_regwrite), .MemRead(id_memread), .MemWrite(id_memwrite), .Branch(id_branch),
    .Jal(id_jal), .Jalr(id_jalr), .ALUSrcA(id_alusrca), .ALUSrcB(id_alusrcb), .ALUOp(id_aluop),
    .ImmSel(id_immsel), .WBSel(id_wbsel), .Halt(id_halt));
  RegisterFile registerfile_1 (
    .clock(clk), .write(wb_en), .rd(wb_rd), .write_data(wb_data), .rs1(id_rs1), .rs2(id_rs2),
    .rs1_data(rf_r1), .rs2_data(rf_r2));
  ImmGen immgen_1 (.Instruction(id_instr), .ImmSel(id_immsel), .Imm(id_imm));
  ALUControl alucontrol_1 (.funct7(id_f7), .ALUOp(id_aluop), .ext3(id_f3), .ALUCtrl(id_aluctrl));
  WBBypass wbbypass_1 (
    .wb_regwrite(wb_en), .wb_rd(wb_rd), .wb_data(wb_data), .rs1(id_rs1), .rs2(id_rs2), .rf_rs1_data(rf_r1),
    .rf_rs2_data(rf_r2), .rs1_data(id_r1), .rs2_data(id_r2));
  HazardUnit hazardunit_1 (.ex_memread(ex_memread), .ex_rd(ex_rd), .id_rs1(id_rs1), .id_rs2(id_rs2), .stall(stall));
  or or_1 (id_flush, stall, flush);
  ID_EX ID_EX (
    .clk(clk), .en(run), .flush(id_flush), .pc(id_pc), .instr(id_instr), .r1(id_r1), .r2(id_r2),
    .imm(id_imm), .rs1(id_rs1), .rs2(id_rs2), .rd(id_rd), .f3(id_f3), .aluctrl(id_aluctrl),
    .alusrca(id_alusrca), .alusrcb(id_alusrcb), .regwrite(id_regwrite), .memread(id_memread),
    .memwrite(id_memwrite), .branch(id_branch), .jal(id_jal), .jalr(id_jalr), .wbsel(id_wbsel),
    .halt(id_halt), .pc_q(ex_pc), .instr_q(ex_instr), .r1_q(ex_r1), .r2_q(ex_r2), .imm_q(ex_imm),
    .rs1_q(ex_rs1), .rs2_q(ex_rs2), .rd_q(ex_rd), .f3_q(ex_f3), .aluctrl_q(ex_aluctrl),
    .alusrca_q(ex_alusrca), .alusrcb_q(ex_alusrcb), .regwrite_q(ex_regwrite), .memread_q(ex_memread),
    .memwrite_q(ex_memwrite), .branch_q(ex_branch), .jal_q(ex_jal), .jalr_q(ex_jalr),
    .wbsel_q({ex_link, ex_wbsel[0]}), .halt_q(ex_halt));
  ForwardingUnit forwardingunit_1 (
    .ex_rs1(ex_rs1), .ex_rs2(ex_rs2), .mem_rd(mem_rd), .mem_regwrite(mem_regwrite), .wb_rd(wb_rd),
    .wb_regwrite(wb_en), .fwdA(fwdA), .fwdB(fwdB));
  Multiplexer #(.select(2), .width(32)) multiplexer_2 (
    .in0(ex_r1), .in1(wb_data), .in2(mem_result), .in3({32{1'b0}}), .out(fa), .sel(fwdA));
  Multiplexer #(.select(2), .width(32)) multiplexer_3 (
    .in0(ex_r2), .in1(wb_data), .in2(mem_result), .in3({32{1'b0}}), .out(fb), .sel(fwdB));
  Multiplexer #(.select(2), .width(32)) multiplexer_4 (
    .in0(fa), .in1(ex_pc), .in2({32{1'b0}}), .in3({32{1'b0}}), .out(alu_a), .sel(ex_alusrca));
  Multiplexer #(.width(32)) multiplexer_5 (.in0(fb), .in1(ex_imm), .out(alu_b), .sel(ex_alusrcb));
  ALU alu_1 (.rs1_data(alu_a), .rs2_data(alu_b), .ALUControl(ex_aluctrl), .result(ex_alu));
  BranchUnit branchunit_1 (.rs1_data(fa), .rs2_data(fb), .ext3(ex_f3), .IsBranch(ex_branch), .branch_taken(ex_taken));
  Adder #(.width(32)) adder_3 (.a(ex_pc), .b(32'h4), .out(ex_pc4));  // open: cin, cout
  Adder #(.width(32)) adder_4 (.a(ex_pc), .b(ex_imm), .out(ex_target));  // open: cin, cout
  assign jalr_target = ex_alu & 32'hfffffffe;  // AND_Gate and_2, 32 bits wide
  or or_2 (flush, ex_taken, ex_jal, ex_jalr);
  Multiplexer #(.width(32)) multiplexer_6 (.in0(ex_alu), .in1(ex_pc4), .out(ex_result), .sel(ex_link));
  Multiplexer #(.width(32)) multiplexer_7 (.in0(ex_target), .in1(jalr_target), .out(redirect_target), .sel(ex_jalr));
  EX_MEM EX_MEM (
    .clk(clk), .en(run), .instr(ex_instr), .result(ex_result), .alu(ex_alu), .sdata(fb), .rd(ex_rd),
    .regwrite(ex_regwrite), .memwrite(ex_memwrite), .wbsel({ex_link, ex_wbsel[0]}), .halt(ex_halt),
    .instr_q(mem_instr), .result_q(mem_result), .alu_q(mem_addr), .sdata_q(mem_wdata), .rd_q(mem_rd),
    .regwrite_q(mem_regwrite), .memwrite_q(mem_memwrite), .wbsel_q(mem_wbsel), .halt_q(mem_halt));
  and and_3 (mem_we, mem_memwrite, run);
  Memory memory_1 (.CLK(clk), .MemWrite(mem_we), .Address(mem_addr), .WriteData(mem_wdata), .ReadData(mem_rdata));
  MEM_WB MEM_WB (
    .clk(clk), .en(run), .instr(mem_instr), .result(mem_result), .rdata(mem_rdata), .rd(mem_rd),
    .regwrite(mem_regwrite), .wbsel(mem_wbsel), .halt(mem_halt), .instr_q(wb_instr), .result_q(wb_result),
    .rdata_q(wb_rdata), .rd_q(wb_rd), .regwrite_q(wb_en), .wbsel_q({wb_wbsel[1], wb_load}), .halt_q(halt));
  Multiplexer #(.width(32)) multiplexer_8 (.in0(wb_result), .in1(wb_rdata), .out(wb_data), .sel(wb_load));

  // Other names for the same wires on the sheet: ex_wbsel[1] = ex_link; mem_alu[31:0] = mem_addr;
  //   mem_sdata[31:0] = mem_wdata; pc[31:0] = out_3; pc_word[9:0] = out_3[11:2]; redirect = flush; wb_halt = halt;
  //   wb_regwrite = wb_en; wb_wbsel[0] = wb_load

  // Notes on the sheet:
  //   IF
  //   contents of IMEM (hex, n*v repeats v):
  //   293 100313 393 1400e13 53a023 628eb3 30293 e8313 438393 fffe0e13 fe0e14e3 ffc3a503 100073
  //   RISC-V RV32I 5-stage pipeline:  IF -> ID -> EX -> MEM -> WB   (forwarding, load-use stall, branch/jump resolved in EX with 2-instruction flush)
  //   ID
  //   EX
  //   MEM
  //   WB
endmodule

module SingleCycleCPU (
  output halt,
  output [31:0] cycle,
  output [31:0] out_3,
  output [31:0] instr,
  output wb_en,
  output [4:0] wb_rd,
  output [31:0] wb_data,
  output mem_we,
  output [31:0] mem_addr,
  output [31:0] mem_wdata
);

  wire ALUSrcB, Branch, clk, Jal, Jalr, run, take_br, taken;
  wire [1:0] ALUOp, ALUSrcA, WBSel;
  wire [2:0] f3, ImmSel;
  wire [3:0] aluctrl;
  wire [4:0] rs1, rs2;
  wire [6:0] f7, op;
  wire [31:0] alu_a, alu_b, br_target, cycle_next, imm, jalr_target, mem_data, pc4, pc_a, pc_next, r1;

  Clock clock_1 (.out(clk));
  Register #(.width(32)) CYCLES (.D(cycle_next), .en(run), .clk(clk), .Q(cycle));  // open: clr
  not not_1 (run, halt);
  Register #(.width(32)) PC (.D(pc_next), .en(run), .clk(clk), .Q(out_3));  // open: clr
  Adder #(.width(32)) adder_1 (.a(cycle), .b(32'h1), .out(cycle_next));  // open: cin, cout
  Adder #(.width(32)) adder_2 (.a(out_3), .b(32'h4), .out(pc4));  // open: cin, cout
  ROM #(.addrWidth(10), .dataWidth(32)) IMEM (.addr(out_3[11:2]), .data(instr));
  InstructionDecode instructiondecode_1 (
    .Instruction(instr), .funct7(f7), .rs2(rs2), .rs1(rs1), .ext3(f3), .rd(wb_rd), .OP(op));
  MainControl maincontrol_1 (
    .OP(op), .RegWrite(wb_en), .MemWrite(mem_we), .Branch(Branch), .Jal(Jal), .Jalr(Jalr), .ALUSrcA(ALUSrcA),
    .ALUSrcB(ALUSrcB), .ALUOp(ALUOp), .ImmSel(ImmSel), .WBSel(WBSel), .Halt(halt));  // open: MemRead
  RegisterFile registerfile_1 (
    .clock(clk), .write(wb_en), .rd(wb_rd), .write_data(wb_data), .rs1(rs1), .rs2(rs2), .rs1_data(r1),
    .rs2_data(mem_wdata));
  ImmGen immgen_1 (.Instruction(instr), .ImmSel(ImmSel), .Imm(imm));
  ALUControl alucontrol_1 (.funct7(f7), .ALUOp(ALUOp), .ext3(f3), .ALUCtrl(aluctrl));
  Multiplexer #(.select(2), .width(32)) multiplexer_1 (
    .in0(r1), .in1(out_3), .in2({32{1'b0}}), .in3({32{1'b0}}), .out(alu_a), .sel(ALUSrcA));
  Multiplexer #(.width(32)) multiplexer_2 (.in0(mem_wdata), .in1(imm), .out(alu_b), .sel(ALUSrcB));
  ALU alu_1 (.rs1_data(alu_a), .rs2_data(alu_b), .ALUControl(aluctrl), .result(mem_addr));
  BranchUnit branchunit_1 (.rs1_data(r1), .rs2_data(mem_wdata), .ext3(f3), .IsBranch(Branch), .branch_taken(taken));
  Adder #(.width(32)) adder_3 (.a(out_3), .b(imm), .out(br_target));  // open: cin, cout
  assign jalr_target = mem_addr & 32'hfffffffe;  // AND_Gate and_1, 32 bits wide
  or or_1 (take_br, taken, Jal);
  Memory memory_1 (.CLK(clk), .MemWrite(mem_we), .Address(mem_addr), .WriteData(mem_wdata), .ReadData(mem_data));
  Multiplexer #(.width(32)) multiplexer_3 (.in0(pc4), .in1(br_target), .out(pc_a), .sel(take_br));
  Multiplexer #(.width(32)) multiplexer_4 (.in0(pc_a), .in1(jalr_target), .out(pc_next), .sel(Jalr));
  Multiplexer #(.select(2), .width(32)) multiplexer_5 (
    .in0(mem_addr), .in1(mem_data), .in2(pc4), .in3({32{1'b0}}), .out(wb_data), .sel(WBSel));

  // Other names for the same wires on the sheet: alu_res[31:0] = mem_addr; MemWrite = mem_we; pc[31:0] = out_3;
  //   pc_word[9:0] = out_3[11:2]; r2[31:0] = mem_wdata; rd[4:0] = wb_rd; RegWrite = wb_en

  // Notes on the sheet:
  //   RISC-V RV32I single-cycle CPU  (program: IMEM ROM, data: DMEM inside Memory)
  //   contents of IMEM (hex, n*v repeats v):
  //   293 100313 393 1400e13 53a023 628eb3 30293 e8313 438393 fffe0e13 fe0e14e3 ffc3a503 100073
endmodule

module ImmGen (
  input  [31:0] Instruction,
  input  [2:0] ImmSel,
  output [31:0] Imm
);

  wire [31:0] immB, immI, immJ, immS;

  assign immI = {{20{Instruction[31]}}, Instruction[31:20]};  // Bit_Extender bit_extender_1
  assign immS = {{20{Instruction[31]}}, {Instruction[31:25], Instruction[11:7]}};  // Bit_Extender bit_extender_2
  assign immB = {{19{Instruction[31]}}, {Instruction[31], Instruction[7], Instruction[30:25], Instruction[11:8], 1'b0}};  // Bit_Extender bit_extender_3
  assign immJ = {{11{Instruction[31]}}, {Instruction[31], Instruction[19:12], Instruction[20], Instruction[30:21], 1'b0}};  // Bit_Extender bit_extender_4
  Multiplexer #(.select(3), .width(32)) multiplexer_1 (
    .in0(immI), .in1(immS), .in2(immB), .in3({Instruction[31:12], {12{1'b0}}}), .in4(immJ), .in5({32{1'b0}}),
    .in6({32{1'b0}}), .in7({32{1'b0}}), .out(Imm), .sel(ImmSel));

  // Other names for the same wires on the sheet: f11_8[3:0] = Instruction[11:8];
  //   immB13[12:1] = {Instruction[31], Instruction[7], Instruction[30:25], Instruction[11:8]};
  //   immS12[11:0] = {Instruction[31:25], Instruction[11:7]}; ins[31:0] = Instruction; f7 = Instruction[7];
  //   f24_21[3:0] = Instruction[24:21]; immI12[11:0] = Instruction[31:20];
  //   immJ21[20:1] = {Instruction[31], Instruction[19:12], Instruction[20], Instruction[30:21]};
  //   immU[31:12] = Instruction[31:12]; f30_25[5:0] = Instruction[30:25]; f20 = Instruction[20];
  //   f19_12[7:0] = Instruction[19:12]; f31 = Instruction[31]; sel[2:0] = ImmSel

  // Notes on the sheet:
  //   Instruction fields
  //   I-type
  //   S-type
  //   B-type
  //   U-type
  //   J-type
endmodule

module RegisterFile (
  input  clock,
  input  write,
  input  [4:0] rd,
  input  [31:0] write_data,
  input  [4:0] rs1,
  input  [4:0] rs2,
  output [31:0] rs1_data,
  output [31:0] rs2_data
);

  wire we1, we2, we3, we4, we5, we6, we7, we8, we9, we10, we11, we12, we13, we14, we15, we16, we17, we18,
       we19, we20, we21, we22, we23, we24, we25, we26, we27, we28, we29, we30, we31;
  wire [31:0] x1, x2, x3, x4, x5, x6, x7, x8, x9, x10, x11, x12, x13, x14, x15, x16, x17, x18, x19, x20, x21,
       x22, x23, x24, x25, x26, x27, x28, x29, x30, x31;

  Decoder #(.select(5)) decoder_1 (
    .out1(we1), .out2(we2), .out3(we3), .out4(we4), .out5(we5), .out6(we6), .out7(we7), .out8(we8),
    .out9(we9), .out10(we10), .out11(we11), .out12(we12), .out13(we13), .out14(we14), .out15(we15),
    .out16(we16), .out17(we17), .out18(we18), .out19(we19), .out20(we20), .out21(we21), .out22(we22),
    .out23(we23), .out24(we24), .out25(we25), .out26(we26), .out27(we27), .out28(we28), .out29(we29),
    .out30(we30), .out31(we31), .sel(rd), .en(write));  // open: out0
  Register #(.width(32)) u_x1 (.D(write_data), .en(we1), .clk(clock), .Q(x1));  // open: clr
  Register #(.width(32)) u_x2 (.D(write_data), .en(we2), .clk(clock), .Q(x2));  // open: clr
  Register #(.width(32)) u_x3 (.D(write_data), .en(we3), .clk(clock), .Q(x3));  // open: clr
  Register #(.width(32)) u_x4 (.D(write_data), .en(we4), .clk(clock), .Q(x4));  // open: clr
  Register #(.width(32)) u_x5 (.D(write_data), .en(we5), .clk(clock), .Q(x5));  // open: clr
  Register #(.width(32)) u_x6 (.D(write_data), .en(we6), .clk(clock), .Q(x6));  // open: clr
  Register #(.width(32)) u_x7 (.D(write_data), .en(we7), .clk(clock), .Q(x7));  // open: clr
  Register #(.width(32)) u_x8 (.D(write_data), .en(we8), .clk(clock), .Q(x8));  // open: clr
  Register #(.width(32)) u_x9 (.D(write_data), .en(we9), .clk(clock), .Q(x9));  // open: clr
  Register #(.width(32)) u_x10 (.D(write_data), .en(we10), .clk(clock), .Q(x10));  // open: clr
  Register #(.width(32)) u_x11 (.D(write_data), .en(we11), .clk(clock), .Q(x11));  // open: clr
  Register #(.width(32)) u_x12 (.D(write_data), .en(we12), .clk(clock), .Q(x12));  // open: clr
  Register #(.width(32)) u_x13 (.D(write_data), .en(we13), .clk(clock), .Q(x13));  // open: clr
  Register #(.width(32)) u_x14 (.D(write_data), .en(we14), .clk(clock), .Q(x14));  // open: clr
  Register #(.width(32)) u_x15 (.D(write_data), .en(we15), .clk(clock), .Q(x15));  // open: clr
  Register #(.width(32)) u_x16 (.D(write_data), .en(we16), .clk(clock), .Q(x16));  // open: clr
  Register #(.width(32)) u_x17 (.D(write_data), .en(we17), .clk(clock), .Q(x17));  // open: clr
  Register #(.width(32)) u_x18 (.D(write_data), .en(we18), .clk(clock), .Q(x18));  // open: clr
  Register #(.width(32)) u_x19 (.D(write_data), .en(we19), .clk(clock), .Q(x19));  // open: clr
  Register #(.width(32)) u_x20 (.D(write_data), .en(we20), .clk(clock), .Q(x20));  // open: clr
  Register #(.width(32)) u_x21 (.D(write_data), .en(we21), .clk(clock), .Q(x21));  // open: clr
  Register #(.width(32)) u_x22 (.D(write_data), .en(we22), .clk(clock), .Q(x22));  // open: clr
  Register #(.width(32)) u_x23 (.D(write_data), .en(we23), .clk(clock), .Q(x23));  // open: clr
  Register #(.width(32)) u_x24 (.D(write_data), .en(we24), .clk(clock), .Q(x24));  // open: clr
  Register #(.width(32)) u_x25 (.D(write_data), .en(we25), .clk(clock), .Q(x25));  // open: clr
  Register #(.width(32)) u_x26 (.D(write_data), .en(we26), .clk(clock), .Q(x26));  // open: clr
  Register #(.width(32)) u_x27 (.D(write_data), .en(we27), .clk(clock), .Q(x27));  // open: clr
  Register #(.width(32)) u_x28 (.D(write_data), .en(we28), .clk(clock), .Q(x28));  // open: clr
  Register #(.width(32)) u_x29 (.D(write_data), .en(we29), .clk(clock), .Q(x29));  // open: clr
  Register #(.width(32)) u_x30 (.D(write_data), .en(we30), .clk(clock), .Q(x30));  // open: clr
  Register #(.width(32)) u_x31 (.D(write_data), .en(we31), .clk(clock), .Q(x31));  // open: clr
  Multiplexer #(.select(5), .width(32)) multiplexer_1 (
    .in0({32{1'b0}}), .in1(x1), .in2(x2), .in3(x3), .in4(x4), .in5(x5), .in6(x6), .in7(x7), .in8(x8),
    .in9(x9), .in10(x10), .in11(x11), .in12(x12), .in13(x13), .in14(x14), .in15(x15), .in16(x16), .in17(x17),
    .in18(x18), .in19(x19), .in20(x20), .in21(x21), .in22(x22), .in23(x23), .in24(x24), .in25(x25),
    .in26(x26), .in27(x27), .in28(x28), .in29(x29), .in30(x30), .in31(x31), .out(rs1_data), .sel(rs1));
  Multiplexer #(.select(5), .width(32)) multiplexer_2 (
    .in0({32{1'b0}}), .in1(x1), .in2(x2), .in3(x3), .in4(x4), .in5(x5), .in6(x6), .in7(x7), .in8(x8),
    .in9(x9), .in10(x10), .in11(x11), .in12(x12), .in13(x13), .in14(x14), .in15(x15), .in16(x16), .in17(x17),
    .in18(x18), .in19(x19), .in20(x20), .in21(x21), .in22(x22), .in23(x23), .in24(x24), .in25(x25),
    .in26(x26), .in27(x27), .in28(x28), .in29(x29), .in30(x30), .in31(x31), .out(rs2_data), .sel(rs2));

  // Other names for the same wires on the sheet: clk = clock; wd[31:0] = write_data; we = write

  // Notes on the sheet:
  //   write-enable decoder
endmodule

module Memory (
  input  CLK,
  input  MemWrite,
  input  [31:0] Address,
  input  [31:0] WriteData,
  output [31:0] ReadData
);

  RAM #(.addrWidth(10), .asyncread("true"), .dataWidth(32)) DMEM (
    .addr(Address[11:2]), .we(MemWrite), .oe(1'b1), .clk(CLK), .din(WriteData), .dout(ReadData));

  // Other names for the same wires on the sheet: addr[31:0] = Address; waddr[9:0] = Address[11:2];
  //   rd[31:0] = ReadData; wd[31:0] = WriteData; we = MemWrite
endmodule

module BranchUnit (
  input  [31:0] rs1_data,
  input  [31:0] rs2_data,
  input  [2:0] ext3,
  input  IsBranch,
  output branch_taken
);

  wire cond, eq, ge, geu, lt, ltu, ne;

  Comparator #(.width(32)) comparator_1 (.a(rs1_data), .b(rs2_data), .eq(eq), .lt(lt));  // open: gt
  Comparator #(.mode("unsigned"), .width(32)) comparator_2 (.a(rs1_data), .b(rs2_data), .lt(ltu));  // open: gt, eq
  not not_1 (ne, eq);
  not not_2 (ge, lt);
  not not_3 (geu, ltu);
  Multiplexer #(.select(3)) multiplexer_1 (
    .in0(eq), .in1(ne), .in2(1'b0), .in3(1'b0), .in4(lt), .in5(ge), .in6(ltu), .in7(geu), .out(cond),
    .sel(ext3));
  and and_1 (branch_taken, cond, IsBranch);

  // Other names for the same wires on the sheet: a[31:0] = rs1_data; b[31:0] = rs2_data; br = IsBranch;
  //   f3[2:0] = ext3; taken = branch_taken
endmodule

module MainControl (
  input  [6:0] OP,
  output RegWrite,
  output MemRead,
  output MemWrite,
  output Branch,
  output Jal,
  output Jalr,
  output [1:0] ALUSrcA,
  output ALUSrcB,
  output [1:0] ALUOp,
  output [2:0] ImmSel,
  output [1:0] WBSel,
  output Halt
);

  wire isI, isR;

  Comparator #(.mode("unsigned"), .width(7)) comparator_1 (.a(OP), .b(7'b0110011), .eq(isR));  // open: gt, lt
  Comparator #(.mode("unsigned"), .width(7)) comparator_2 (.a(OP), .b(7'b0010011), .eq(isI));  // open: gt, lt
  Comparator #(.mode("unsigned"), .width(7)) comparator_3 (.a(OP), .b(7'b0000011), .eq(MemRead));  // open: gt, lt
  Comparator #(.mode("unsigned"), .width(7)) comparator_4 (.a(OP), .b(7'b0100011), .eq(MemWrite));  // open: gt, lt
  Comparator #(.mode("unsigned"), .width(7)) comparator_5 (.a(OP), .b(7'b1100011), .eq(Branch));  // open: gt, lt
  Comparator #(.mode("unsigned"), .width(7)) comparator_6 (.a(OP), .b(7'b1101111), .eq(ImmSel[2]));  // open: gt, lt
  Comparator #(.mode("unsigned"), .width(7)) comparator_7 (.a(OP), .b(7'b1100111), .eq(Jalr));  // open: gt, lt
  Comparator #(.mode("unsigned"), .width(7)) comparator_8 (.a(OP), .b(7'b0110111), .eq(ALUSrcA[1]));  // open: gt, lt
  Comparator #(.mode("unsigned"), .width(7)) comparator_9 (.a(OP), .b(7'b0010111), .eq(ALUSrcA[0]));  // open: gt, lt
  Comparator #(.mode("unsigned"), .width(7)) comparator_10 (.a(OP), .b(7'b1110011), .eq(Halt));  // open: gt, lt
  or or_1 (RegWrite, isR, isI, MemRead, ImmSel[2], Jalr, ALUSrcA[1], ALUSrcA[0]);
  or or_2 (ALUSrcB, isI, MemRead, MemWrite, Jalr, ALUSrcA[1], ALUSrcA[0]);
  or or_3 (ALUOp[0], isI, Branch);
  or or_4 (ALUOp[1], isR, isI);
  or or_5 (ImmSel[0], MemWrite, ALUSrcA[1], ALUSrcA[0]);
  or or_6 (ImmSel[1], Branch, ALUSrcA[1], ALUSrcA[0]);
  or or_7 (WBSel[1], ImmSel[2], Jalr);

  assign Jal = ImmSel[2];
  assign WBSel[0] = MemRead;

  // Other names for the same wires on the sheet: isAuipc = ALUSrcA[0]; isLui = ALUSrcA[1]; imm0 = ImmSel[0];
  //   imm1 = ImmSel[1]; isJal = ImmSel[2]; isBranch = Branch; isJalr = Jalr; isStore = MemWrite; isSys = Halt;
  //   isLoad = MemRead; wb1 = WBSel[1]

  // Notes on the sheet:
  //   R = 0x33
  //   I = 0x13
  //   Load = 0x03
  //   Store = 0x23
  //   Branch = 0x63
  //   Jal = 0x6F
  //   Jalr = 0x67
  //   Lui = 0x37
  //   Auipc = 0x17
  //   Sys = 0x73
endmodule

module HazardUnit (
  input  ex_memread,
  input  [4:0] ex_rd,
  input  [4:0] id_rs1,
  input  [4:0] id_rs2,
  output stall
);

  wire m1, m2, rd_nz, rd_zero, uses;

  Comparator #(.mode("unsigned"), .width(5)) comparator_1 (.a(ex_rd), .b(id_rs1), .eq(m1));  // open: gt, lt
  Comparator #(.mode("unsigned"), .width(5)) comparator_2 (.a(ex_rd), .b(id_rs2), .eq(m2));  // open: gt, lt
  Comparator #(.mode("unsigned"), .width(5)) comparator_3 (.a(ex_rd), .b({5{1'b0}}), .eq(rd_zero));  // open: gt, lt
  or or_1 (uses, m1, m2);
  not not_1 (rd_nz, rd_zero);
  and and_1 (stall, ex_memread, uses, rd_nz);

  // Other names for the same wires on the sheet: memread = ex_memread; rs1[4:0] = id_rs1; rs2[4:0] = id_rs2
endmodule

module ForwardingUnit (
  input  [4:0] ex_rs1,
  input  [4:0] ex_rs2,
  input  [4:0] mem_rd,
  input  mem_regwrite,
  input  [4:0] wb_rd,
  input  wb_regwrite,
  output [1:0] fwdA,
  output [1:0] fwdB
);

  wire a_mem_eq, a_wb_eq, b_mem_eq, b_wb_eq, mem_ok, mem_rd0, wb_ok, wb_rd0;

  Comparator #(.mode("unsigned"), .width(5)) comparator_1 (.a(mem_rd), .b(ex_rs1), .eq(a_mem_eq));  // open: gt, lt
  Comparator #(.mode("unsigned"), .width(5)) comparator_2 (.a(wb_rd), .b(ex_rs1), .eq(a_wb_eq));  // open: gt, lt
  Comparator #(.mode("unsigned"), .width(5)) comparator_3 (.a(mem_rd), .b(ex_rs2), .eq(b_mem_eq));  // open: gt, lt
  Comparator #(.mode("unsigned"), .width(5)) comparator_4 (.a(wb_rd), .b(ex_rs2), .eq(b_wb_eq));  // open: gt, lt
  Comparator #(.mode("unsigned"), .width(5)) comparator_5 (.a(mem_rd), .b({5{1'b0}}), .eq(mem_rd0));  // open: gt, lt
  Comparator #(.mode("unsigned"), .width(5)) comparator_6 (.a(wb_rd), .b({5{1'b0}}), .eq(wb_rd0));  // open: gt, lt
  and and_1 (mem_ok, mem_regwrite, ~mem_rd0);  // AND_Gate
  and and_2 (wb_ok, wb_regwrite, ~wb_rd0);  // AND_Gate
  and and_3 (fwdA[1], mem_ok, a_mem_eq);
  and and_4 (fwdA[0], wb_ok, a_wb_eq, ~fwdA[1]);  // AND_Gate
  and and_5 (fwdB[1], mem_ok, b_mem_eq);
  and and_6 (fwdB[0], wb_ok, b_wb_eq, ~fwdB[1]);  // AND_Gate

  // Other names for the same wires on the sheet: a_wb = fwdA[0]; a_mem = fwdA[1]; b_wb = fwdB[0]; b_mem = fwdB[1];
  //   mem_rw = mem_regwrite; rs1[4:0] = ex_rs1; rs2[4:0] = ex_rs2; wb_rw = wb_regwrite
endmodule

module WBBypass (
  input  wb_regwrite,
  input  [4:0] wb_rd,
  input  [31:0] wb_data,
  input  [4:0] rs1,
  input  [4:0] rs2,
  input  [31:0] rf_rs1_data,
  input  [31:0] rf_rs2_data,
  output [31:0] rs1_data,
  output [31:0] rs2_data
);

  wire eq1, eq2, ok, rd0, sel1, sel2;

  Comparator #(.mode("unsigned"), .width(5)) comparator_1 (.a(wb_rd), .b({5{1'b0}}), .eq(rd0));  // open: gt, lt
  Comparator #(.mode("unsigned"), .width(5)) comparator_2 (.a(wb_rd), .b(rs1), .eq(eq1));  // open: gt, lt
  Comparator #(.mode("unsigned"), .width(5)) comparator_3 (.a(wb_rd), .b(rs2), .eq(eq2));  // open: gt, lt
  and and_1 (ok, wb_regwrite, ~rd0);  // AND_Gate
  and and_2 (sel1, ok, eq1);
  and and_3 (sel2, ok, eq2);
  Multiplexer #(.width(32)) multiplexer_1 (.in0(rf_rs1_data), .in1(wb_data), .out(rs1_data), .sel(sel1));
  Multiplexer #(.width(32)) multiplexer_2 (.in0(rf_rs2_data), .in1(wb_data), .out(rs2_data), .sel(sel2));

  // Other names for the same wires on the sheet: o1[31:0] = rs1_data; o2[31:0] = rs2_data; rd[4:0] = wb_rd;
  //   rf1[31:0] = rf_rs1_data; rf2[31:0] = rf_rs2_data; rw = wb_regwrite; wd[31:0] = wb_data
endmodule

module IF_ID (
  input  clk,
  input  en,
  input  flush,
  input  [31:0] pc,
  input  [31:0] instr,
  output [31:0] pc_q,
  output [31:0] instr_q
);

  wire [31:0] instr_d, pc_d;

  Multiplexer #(.width(32)) multiplexer_1 (.in0(pc), .in1({32{1'b0}}), .out(pc_d), .sel(flush));
  Multiplexer #(.width(32)) multiplexer_2 (.in0(instr), .in1({32{1'b0}}), .out(instr_d), .sel(flush));
  Register #(.width(32)) register_1 (.D(pc_d), .en(en), .clk(clk), .Q(pc_q));  // open: clr
  Register #(.width(32)) register_2 (.D(instr_d), .en(en), .clk(clk), .Q(instr_q));  // open: clr

  // Other names for the same wires on the sheet: instr_in[31:0] = instr; pc_in[31:0] = pc
endmodule

module ID_EX (
  input  clk,
  input  en,
  input  flush,
  input  [31:0] pc,
  input  [31:0] instr,
  input  [31:0] r1,
  input  [31:0] r2,
  input  [31:0] imm,
  input  [4:0] rs1,
  input  [4:0] rs2,
  input  [4:0] rd,
  input  [2:0] f3,
  input  [3:0] aluctrl,
  input  [1:0] alusrca,
  input  alusrcb,
  input  regwrite,
  input  memread,
  input  memwrite,
  input  branch,
  input  jal,
  input  jalr,
  input  [1:0] wbsel,
  input  halt,
  output [31:0] pc_q,
  output [31:0] instr_q,
  output [31:0] r1_q,
  output [31:0] r2_q,
  output [31:0] imm_q,
  output [4:0] rs1_q,
  output [4:0] rs2_q,
  output [4:0] rd_q,
  output [2:0] f3_q,
  output [3:0] aluctrl_q,
  output [1:0] alusrca_q,
  output alusrcb_q,
  output regwrite_q,
  output memread_q,
  output memwrite_q,
  output branch_q,
  output jal_q,
  output jalr_q,
  output [1:0] wbsel_q,
  output halt_q
);

  wire alusrcb_d, branch_d, halt_d, jal_d, jalr_d, memread_d, memwrite_d, regwrite_d;
  wire [1:0] alusrca_d, wbsel_d;
  wire [2:0] f3_d;
  wire [3:0] aluctrl_d;
  wire [4:0] rd_d, rs1_d, rs2_d;
  wire [31:0] imm_d, instr_d, pc_d, r1_d, r2_d;

  Multiplexer #(.width(32)) multiplexer_1 (.in0(pc), .in1({32{1'b0}}), .out(pc_d), .sel(flush));
  Multiplexer #(.width(32)) multiplexer_2 (.in0(instr), .in1({32{1'b0}}), .out(instr_d), .sel(flush));
  Multiplexer #(.width(32)) multiplexer_3 (.in0(r1), .in1({32{1'b0}}), .out(r1_d), .sel(flush));
  Multiplexer #(.width(32)) multiplexer_4 (.in0(r2), .in1({32{1'b0}}), .out(r2_d), .sel(flush));
  Multiplexer #(.width(32)) multiplexer_5 (.in0(imm), .in1({32{1'b0}}), .out(imm_d), .sel(flush));
  Multiplexer #(.width(5)) multiplexer_6 (.in0(rs1), .in1({5{1'b0}}), .out(rs1_d), .sel(flush));
  Multiplexer #(.width(5)) multiplexer_7 (.in0(rs2), .in1({5{1'b0}}), .out(rs2_d), .sel(flush));
  Multiplexer #(.width(5)) multiplexer_8 (.in0(rd), .in1({5{1'b0}}), .out(rd_d), .sel(flush));
  Multiplexer #(.width(3)) multiplexer_9 (.in0(f3), .in1(3'b000), .out(f3_d), .sel(flush));
  Multiplexer #(.width(4)) multiplexer_10 (.in0(aluctrl), .in1(4'b0000), .out(aluctrl_d), .sel(flush));
  Multiplexer #(.width(2)) multiplexer_11 (.in0(alusrca), .in1(2'b00), .out(alusrca_d), .sel(flush));
  Multiplexer multiplexer_12 (.in0(alusrcb), .in1(1'b0), .out(alusrcb_d), .sel(flush));
  Multiplexer multiplexer_13 (.in0(regwrite), .in1(1'b0), .out(regwrite_d), .sel(flush));
  Multiplexer multiplexer_14 (.in0(memread), .in1(1'b0), .out(memread_d), .sel(flush));
  Multiplexer multiplexer_15 (.in0(memwrite), .in1(1'b0), .out(memwrite_d), .sel(flush));
  Multiplexer multiplexer_16 (.in0(branch), .in1(1'b0), .out(branch_d), .sel(flush));
  Multiplexer multiplexer_17 (.in0(jal), .in1(1'b0), .out(jal_d), .sel(flush));
  Multiplexer multiplexer_18 (.in0(jalr), .in1(1'b0), .out(jalr_d), .sel(flush));
  Multiplexer #(.width(2)) multiplexer_19 (.in0(wbsel), .in1(2'b00), .out(wbsel_d), .sel(flush));
  Multiplexer multiplexer_20 (.in0(halt), .in1(1'b0), .out(halt_d), .sel(flush));
  Register #(.width(32)) register_1 (.D(pc_d), .en(en), .clk(clk), .Q(pc_q));  // open: clr
  Register #(.width(32)) register_2 (.D(instr_d), .en(en), .clk(clk), .Q(instr_q));  // open: clr
  Register #(.width(32)) register_3 (.D(r1_d), .en(en), .clk(clk), .Q(r1_q));  // open: clr
  Register #(.width(32)) register_4 (.D(r2_d), .en(en), .clk(clk), .Q(r2_q));  // open: clr
  Register #(.width(32)) register_5 (.D(imm_d), .en(en), .clk(clk), .Q(imm_q));  // open: clr
  Register #(.width(5)) register_6 (.D(rs1_d), .en(en), .clk(clk), .Q(rs1_q));  // open: clr
  Register #(.width(5)) register_7 (.D(rs2_d), .en(en), .clk(clk), .Q(rs2_q));  // open: clr
  Register #(.width(5)) register_8 (.D(rd_d), .en(en), .clk(clk), .Q(rd_q));  // open: clr
  Register #(.width(3)) register_9 (.D(f3_d), .en(en), .clk(clk), .Q(f3_q));  // open: clr
  Register #(.width(4)) register_10 (.D(aluctrl_d), .en(en), .clk(clk), .Q(aluctrl_q));  // open: clr
  Register #(.width(2)) register_11 (.D(alusrca_d), .en(en), .clk(clk), .Q(alusrca_q));  // open: clr
  Register #(.width(1)) register_12 (.D(alusrcb_d), .en(en), .clk(clk), .Q(alusrcb_q));  // open: clr
  Register #(.width(1)) register_13 (.D(regwrite_d), .en(en), .clk(clk), .Q(regwrite_q));  // open: clr
  Register #(.width(1)) register_14 (.D(memread_d), .en(en), .clk(clk), .Q(memread_q));  // open: clr
  Register #(.width(1)) register_15 (.D(memwrite_d), .en(en), .clk(clk), .Q(memwrite_q));  // open: clr
  Register #(.width(1)) register_16 (.D(branch_d), .en(en), .clk(clk), .Q(branch_q));  // open: clr
  Register #(.width(1)) register_17 (.D(jal_d), .en(en), .clk(clk), .Q(jal_q));  // open: clr
  Register #(.width(1)) register_18 (.D(jalr_d), .en(en), .clk(clk), .Q(jalr_q));  // open: clr
  Register #(.width(2)) register_19 (.D(wbsel_d), .en(en), .clk(clk), .Q(wbsel_q));  // open: clr
  Register #(.width(1)) register_20 (.D(halt_d), .en(en), .clk(clk), .Q(halt_q));  // open: clr

  // Other names for the same wires on the sheet: aluctrl_in[3:0] = aluctrl; alusrca_in[1:0] = alusrca;
  //   alusrcb_in = alusrcb; branch_in = branch; f3_in[2:0] = f3; halt_in = halt; imm_in[31:0] = imm;
  //   instr_in[31:0] = instr; jal_in = jal; jalr_in = jalr; memread_in = memread; memwrite_in = memwrite;
  //   pc_in[31:0] = pc; r1_in[31:0] = r1; r2_in[31:0] = r2; rd_in[4:0] = rd; regwrite_in = regwrite;
  //   rs1_in[4:0] = rs1; rs2_in[4:0] = rs2; wbsel_in[1:0] = wbsel
endmodule

module EX_MEM (
  input  clk,
  input  en,
  input  [31:0] instr,
  input  [31:0] result,
  input  [31:0] alu,
  input  [31:0] sdata,
  input  [4:0] rd,
  input  regwrite,
  input  memwrite,
  input  [1:0] wbsel,
  input  halt,
  output [31:0] instr_q,
  output [31:0] result_q,
  output [31:0] alu_q,
  output [31:0] sdata_q,
  output [4:0] rd_q,
  output regwrite_q,
  output memwrite_q,
  output [1:0] wbsel_q,
  output halt_q
);

  Register #(.width(32)) register_1 (.D(instr), .en(en), .clk(clk), .Q(instr_q));  // open: clr
  Register #(.width(32)) register_2 (.D(result), .en(en), .clk(clk), .Q(result_q));  // open: clr
  Register #(.width(32)) register_3 (.D(alu), .en(en), .clk(clk), .Q(alu_q));  // open: clr
  Register #(.width(32)) register_4 (.D(sdata), .en(en), .clk(clk), .Q(sdata_q));  // open: clr
  Register #(.width(5)) register_5 (.D(rd), .en(en), .clk(clk), .Q(rd_q));  // open: clr
  Register #(.width(1)) register_6 (.D(regwrite), .en(en), .clk(clk), .Q(regwrite_q));  // open: clr
  Register #(.width(1)) register_7 (.D(memwrite), .en(en), .clk(clk), .Q(memwrite_q));  // open: clr
  Register #(.width(2)) register_8 (.D(wbsel), .en(en), .clk(clk), .Q(wbsel_q));  // open: clr
  Register #(.width(1)) register_9 (.D(halt), .en(en), .clk(clk), .Q(halt_q));  // open: clr

  // Other names for the same wires on the sheet: alu_in[31:0] = alu; halt_in = halt; instr_in[31:0] = instr;
  //   memwrite_in = memwrite; rd_in[4:0] = rd; regwrite_in = regwrite; result_in[31:0] = result;
  //   sdata_in[31:0] = sdata; wbsel_in[1:0] = wbsel
endmodule

module MEM_WB (
  input  clk,
  input  en,
  input  [31:0] instr,
  input  [31:0] result,
  input  [31:0] rdata,
  input  [4:0] rd,
  input  regwrite,
  input  [1:0] wbsel,
  input  halt,
  output [31:0] instr_q,
  output [31:0] result_q,
  output [31:0] rdata_q,
  output [4:0] rd_q,
  output regwrite_q,
  output [1:0] wbsel_q,
  output halt_q
);

  Register #(.width(32)) register_1 (.D(instr), .en(en), .clk(clk), .Q(instr_q));  // open: clr
  Register #(.width(32)) register_2 (.D(result), .en(en), .clk(clk), .Q(result_q));  // open: clr
  Register #(.width(32)) register_3 (.D(rdata), .en(en), .clk(clk), .Q(rdata_q));  // open: clr
  Register #(.width(5)) register_4 (.D(rd), .en(en), .clk(clk), .Q(rd_q));  // open: clr
  Register #(.width(1)) register_5 (.D(regwrite), .en(en), .clk(clk), .Q(regwrite_q));  // open: clr
  Register #(.width(2)) register_6 (.D(wbsel), .en(en), .clk(clk), .Q(wbsel_q));  // open: clr
  Register #(.width(1)) register_7 (.D(halt), .en(en), .clk(clk), .Q(halt_q));  // open: clr

  // Other names for the same wires on the sheet: halt_in = halt; instr_in[31:0] = instr; rd_in[4:0] = rd;
  //   rdata_in[31:0] = rdata; regwrite_in = regwrite; result_in[31:0] = result; wbsel_in[1:0] = wbsel
endmodule

module ALU (
  input  [31:0] rs1_data,
  input  [31:0] rs2_data,
  input  [3:0] ALUControl,
  output [31:0] result
);

  wire comparator_1_lt, comparator_2_lt;
  wire [31:0] adder_1_out, and_1_out, bit_extender_1_out, bit_extender_2_out, or_1_out, shifter_1_out,
       shifter_2_out, shifter_3_out, subtractor_1_out, xor_1_out;

  Adder #(.width(32)) adder_1 (.a(rs1_data), .b(rs2_data), .out(adder_1_out));  // open: cin, cout
  Subtractor #(.width(32)) subtractor_1 (.a(rs1_data), .b(rs2_data), .out(subtractor_1_out));  // open: bin, bout
  assign and_1_out = rs1_data & rs2_data;  // AND_Gate and_1, 32 bits wide
  assign or_1_out = rs1_data | rs2_data;  // OR_Gate or_1, 32 bits wide
  assign xor_1_out = rs1_data ^ rs2_data;  // XOR_Gate xor_1, 32 bits wide
  Shifter #(.width(32)) shifter_1 (.in(rs1_data), .\dist (rs2_data[4:0]), .out(shifter_1_out));
  Shifter #(.shift("lr"), .width(32)) shifter_2 (.in(rs1_data), .\dist (rs2_data[4:0]), .out(shifter_2_out));
  Shifter #(.shift("ar"), .width(32)) shifter_3 (.in(rs1_data), .\dist (rs2_data[4:0]), .out(shifter_3_out));
  Comparator #(.width(32)) comparator_1 (.a(rs1_data), .b(rs2_data), .lt(comparator_1_lt));  // open: gt, eq
  Comparator #(.mode("unsigned"), .width(32)) comparator_2 (
    .a(rs1_data), .b(rs2_data), .lt(comparator_2_lt));  // open: gt, eq
  assign bit_extender_1_out = {{31{1'b0}}, comparator_1_lt};  // Bit_Extender bit_extender_1
  assign bit_extender_2_out = {{31{1'b0}}, comparator_2_lt};  // Bit_Extender bit_extender_2
  Multiplexer #(.select(4), .width(32)) multiplexer_1 (
    .in0(adder_1_out), .in1(subtractor_1_out), .in2(and_1_out), .in3(or_1_out), .in4(xor_1_out),
    .in5(shifter_1_out), .in6(shifter_2_out), .in7(shifter_3_out), .in8(bit_extender_1_out),
    .in9(bit_extender_2_out), .out(result), .sel(ALUControl));  // open: in10, in11, in12, in13, in14, in15
endmodule

module ALUControl (
  input  [6:0] funct7,
  input  [1:0] ALUOp,
  input  [2:0] ext3,
  output [3:0] ALUCtrl
);

  wire [3:0] multiplexer_1_out, multiplexer_2_out, multiplexer_3_out, multiplexer_4_out;

  Multiplexer #(.width(4)) multiplexer_1 (.in0(4'b0110), .in1(4'b0111), .out(multiplexer_1_out), .sel(funct7[5]));
  Multiplexer #(.width(4)) multiplexer_2 (.in0(4'b0000), .in1(4'b0001), .out(multiplexer_2_out), .sel(funct7[5]));
  Multiplexer #(.select(3), .width(4)) multiplexer_3 (
    .in0(4'b0000), .in1(4'b0101), .in2(4'b1000), .in3(4'b1001), .in4(4'b0100), .in5(multiplexer_1_out),
    .in6(4'b0011), .in7(4'b0010), .out(multiplexer_3_out), .sel(ext3));
  Multiplexer #(.select(3), .width(4)) multiplexer_4 (
    .in0(multiplexer_2_out), .in1(4'b0101), .in2(4'b1000), .in3(4'b1001), .in4(4'b0100),
    .in5(multiplexer_1_out), .in6(4'b0011), .in7(4'b0010), .out(multiplexer_4_out), .sel(ext3));
  Multiplexer #(.select(2), .width(4)) multiplexer_5 (
    .in0(4'b0000), .in1(4'b0001), .in2(multiplexer_4_out), .in3(multiplexer_3_out), .out(ALUCtrl), .sel(ALUOp));

  // Notes on the sheet:
  //   ADD
  //   SUB
endmodule

module InstructionDecode (
  input  [31:0] Instruction,
  output [6:0] funct7,
  output [4:0] rs2,
  output [4:0] rs1,
  output [2:0] ext3,
  output [4:0] rd,
  output [6:0] OP
);


  assign ext3 = Instruction[14:12];
  assign funct7 = Instruction[31:25];
  assign OP = Instruction[6:0];
  assign rd = Instruction[11:7];
  assign rs1 = Instruction[19:15];
  assign rs2 = Instruction[24:20];
endmodule
